# Fritzing sketch 20190501_electric_tap_v1 (saved by Fritzing 0.9.3b)

parts:
  TIP120_1 = npn-Powertransistor [package="TO220 [THT]"]
  TIP120_3 = npn-Powertransistor [package="TO220 [THT]"]
  TIP120_2 = npn-Powertransistor [package="TO220 [THT]"]
  U2 = Sharp PC817 [package=THT]
  PC817 = Sharp PC817 [package=THT]
  R1 = Resistor [tolerance=±5% resistance=1k package="0603 [SMD]"]
  R2 = Resistor [tolerance=±5% resistance=1k package="0603 [SMD]"]
  R3 = Resistor [tolerance=±5% resistance=1k package="0603 [SMD]"]
  R4 = Resistor [tolerance=±5% resistance=220 package="0603 [SMD]"]
  R5 = Resistor [tolerance=±5% resistance=220 package="0603 [SMD]"]
  R6 = Resistor [tolerance=±5% resistance=220 package="0603 [SMD]"]
  TAP3 = Solenoid
  TAP2 = Solenoid
  U1 = Sharp PC817 [package=THT]
  V5 = DC Power [voltage=5V]
  V6 = DC Power [voltage=12V]
  TAP1 = Solenoid
  S1 = Toggle Switch [package=THT]
  S2 = Toggle Switch [package=THT]
  S3 = Toggle Switch [package=THT]
  R7 = Resistor [tolerance=±5% resistance=2.2k package="0603 [SMD]"]

nets:
  N1: TIP120_1.base, R2.Pin_1
  N2: TIP120_1.collector, TAP1.pin1
  N3: TIP120_1.emitter, TIP120_3.emitter, TIP120_2.emitter, V6.V-
  N4: TIP120_3.base, R3.Pin_1
  N5: TIP120_3.collector, TAP3.pin1
  N6: TIP120_2.base, R1.Pin_1
  N7: TIP120_2.collector, TAP2.pin1
  N8: U2.Pin_1, R5.Pin_1, S2.L1
  N9: U2.Pin_2, PC817.Pin_2, U1.Pin_2, V5.V-
  N10: U2.Pin_4, PC817.Pin_4, TAP3.pin2, TAP2.pin2, U1.Pin_4, V6.V+, TAP1.pin2
  N11: U2.Pin_3, R1.Pin_0
  N12: PC817.Pin_1, R4.Pin_1, S3.L1
  N13: PC817.Pin_3, R3.Pin_0
  N14: R2.Pin_0, U1.Pin_3
  N15: R6.Pin_1, U1.Pin_1, S1.L1
  N16: S1.COM, S2.COM, S3.COM, R7.Pin_0

notes:
  12+
  12GND
  3.3GND
  D1 3.3+ (IN)
  D2 3.3+ (IN)
  D3 3.3+ (IN)
  3.3+

// code stored in the sketch: 20190501_electric_tap_v1.ino

